# Fritzing sketch warmachine (saved by Fritzing 0.9.3b)
breadboards: 1

parts:
  LED1 = smd LED [color="Red (633nm)" package="0603 [SMD]"]
  LED2 = smd LED [color="Red (633nm)" package="0603 [SMD]"]
  S1 = Pushbutton [package="[THT]"]
  WeMos_D1_Mini1 = WeMos D1 Mini
  J1 = Basic Servo
  J2 = Basic Servo
  VCC1 = 4 x AAA Battery Mount
  R1 = Resistor [tolerance=±5% resistance=220 package="2512 [SMD]"]
  R2 = Resistor [tolerance=±5% resistance=220 package="2512 [SMD]"]

nets:
  GND: LED1.cathode, LED2.cathode, S1.Pin_1, S1.Pin_2, WeMos_D1_Mini1.G, J1.gnd, J2.gnd, VCC1.-, R1.Pin_0
  N1: LED1.anode, WeMos_D1_Mini1.D4
  N2: LED2.anode, WeMos_D1_Mini1.D3
  N3: S1.Pin_3, WeMos_D1_Mini1.D2
  VCC: WeMos_D1_Mini1.5V, J1.vcc, J2.vcc, VCC1.+, R2.Pin_0
  N4: WeMos_D1_Mini1.RST, R1.Pin_1, R2.Pin_1

notes:
  Helmet
